// Logisim project brainfuck_machine.circ as structural Verilog: 4 circuits, main circuit main
module main (
  input  CONTROL_RESET,
  input  CONTROL_CLOCK,
  input  CONTROL_ENABLE,
  input  WRITE_DATA,
  input  WRITE_CLOCK,
  input  WRITE_ENABLE,
  output OUTPUT_READY,
  output AWAITING_INPUT,
  output [7:0] ROM_DATA,
  output ROM_CHIP_ENABLE,
  output ROM_WRITE_ENABLE
);

  wire and_1_out, and_2_out, and_3_out, and_4_out, and_5_out, and_6_out, and_8_out, and_9_out, and_10_out,
       and_11_out, and_12_out, and_13_out, and_14_out, and_15_out, and_16_out, and_17_out, and_18_out,
       and_19_out, and_20_out, and_21_out, and_22_out, and_23_out, clock_1_out, comparator_1_eq,
       comparator_11_eq, comparator_12_eq, controlled_buffer_1_out, controlled_buffer_2_out,
       controlled_buffer_3_out, controlled_buffer_6_out, counter_3_carry, EXT_RESET_out, j_k_ff_1_q,
       j_k_ff_1_qn, j_k_ff_2_q, j_k_ff_3_q, j_k_ff_4_qn, j_k_ff_5_q, j_k_ff_5_qn, j_k_ff_6_qn, j_k_ff_7_qn,
       monostable_1_pulse, monostable_2_pulse, monostable_3_pulse, monostable_4_pulse, monostable_5_pulse,
       monostable_6_pulse, monostable_7_pulse, monostable_8_pulse, nor_1_out, nor_2_out, nor_3_out,
       nor_4_out, not_1_out, not_2_out, not_3_out, not_4_out, not_5_out, not_6_out, not_7_out, not_8_out,
       not_9_out, not_10_out, not_11_out, not_12_out, not_13_out, or_2_out, or_3_out, or_4_out, or_5_out,
       or_7_out, or_8_out, or_9_out, or_10_out, pull_resistor_9_node, RESET_out, s_r_ff_1_q, s_r_ff_1_qn,
       slow_clock_1_out_2, TURTLE_p2;
  wire [2:2] pull_resistor_8_node;
  wire [3:0] counter_1_q, ram_1_data, ram_1_data_2;
  wire [5:0] comparator_10_eq;
  wire [6:0] bit_extender_4_out, keyboard_1_data;
  wire [7:0] adder_1_out, comparator_9_eq, controlled_buffer_12_out, controlled_buffer_19_out, R_IN_q,
       R_OUT_q, register_1_q, register_2_q, rom_1_data, subtractor_1_out, undriven;
  wire [8:0] PUSH_INPUT_out;
  wire [13:0] adder_2_out, counter_4_q, Jump_Snapshot_q;
  wire [14:0] counter_2_q, counter_3_q, ram_2_data;
  wire [15:0] bit_extender_1_out, bit_extender_2_out;

  Button RESET (.out(RESET_out));
  // Switch TURTLE: pin names not known; wires that end beside it: 1'b1, TURTLE_p2
  assign controlled_buffer_1_out = not_1_out ? RESET_out : 1'bz;  // Controlled_Buffer controlled_buffer_1
  Pull_Resistor pull_resistor_1 (.node(TURTLE_p2));
  Pull_Resistor pull_resistor_2 (.node(WRITE_DATA));
  Pull_Resistor pull_resistor_3 (.node(WRITE_CLOCK));
  Pull_Resistor pull_resistor_4 (.node(WRITE_ENABLE));
  Pull_Resistor pull_resistor_5 (.node(CONTROL_RESET));
  assign controlled_buffer_2_out = CONTROL_ENABLE ? CONTROL_RESET : 1'bz;  // Controlled_Buffer controlled_buffer_2
  Pull_Resistor pull_resistor_6 (.node(CONTROL_CLOCK));
  Pull_Resistor pull_resistor_7 (.node(CONTROL_ENABLE));
  not not_1 (not_1_out, CONTROL_ENABLE);
  or or_1 (controlled_buffer_2_out, controlled_buffer_1_out, or_4_out);
  monostable monostable_1 (.WAVE(controlled_buffer_2_out), .PULSE(monostable_1_pulse));
  Clock clock_1 (.out(clock_1_out));
  slow_clock slow_clock_1 (.RESET(monostable_1_pulse), .out_2(slow_clock_1_out_2));
  // Shift_Register shift_register_1: pin names not known; wires that end beside it: monostable_1_pulse, WRITE_ENABLE, WRITE_CLOCK, WRITE_DATA
  J_K_Flip_Flop #(.trigger("falling")) j_k_ff_1 (
    .J(and_1_out), .K(1'b0), .clk(s_r_ff_1_q), .Q(j_k_ff_1_q), .Qn(j_k_ff_1_qn), .reset(monostable_1_pulse));  // open: preset
  and and_1 (and_1_out, counter_3_carry, j_k_ff_1_qn);
  J_K_Flip_Flop j_k_ff_2 (
    .J(j_k_ff_1_q), .K(1'b0), .clk(s_r_ff_1_q), .Q(j_k_ff_2_q), .Qn(comparator_10_eq[4]),
    .reset(monostable_1_pulse));  // open: preset
  not not_2 (not_2_out, WRITE_ENABLE);
  monostable monostable_2 (.WAVE(WRITE_ENABLE), .PULSE(monostable_2_pulse));
  monostable monostable_3 (.WAVE(not_2_out), .PULSE(monostable_3_pulse));
  or or_2 (or_2_out, TURTLE_p2, or_3_out);
  or or_3 (or_3_out, CONTROL_ENABLE, WRITE_ENABLE);
  not not_3 (not_3_out, or_3_out);
  not not_4 (not_4_out, WRITE_ENABLE);
  or or_4 (or_4_out, monostable_2_pulse, monostable_3_pulse);
  and and_2 (and_2_out, j_k_ff_1_q, or_2_out);
  not not_5 (not_5_out, and_2_out);
  and and_3 (and_3_out, not_3_out, j_k_ff_1_q, TURTLE_p2);
  and and_4 (and_4_out, not_4_out, j_k_ff_1_q, CONTROL_ENABLE);
  Counter #(.max('hf), .width(4)) counter_1 (
    .clr(monostable_1_pulse), .load(comparator_1_eq), .count(WRITE_ENABLE), .clk(WRITE_CLOCK), .D(4'b0001),
    .Q(counter_1_q));  // open: up, carry
  nor nor_1 (nor_1_out, comparator_10_eq[0], comparator_10_eq[4], comparator_10_eq[1], AWAITING_INPUT);
  nor nor_2 (nor_2_out, comparator_10_eq[1], and_20_out, comparator_10_eq[3]);
  assign controlled_buffer_3_out = not_5_out ? clock_1_out : 1'bz;  // Controlled_Buffer controlled_buffer_3
  assign controlled_buffer_3_out = and_3_out ? slow_clock_1_out_2 : 1'bz;  // Controlled_Buffer controlled_buffer_4
  assign controlled_buffer_3_out = and_4_out ? CONTROL_CLOCK : 1'bz;  // Controlled_Buffer controlled_buffer_5
  not not_6 (not_6_out, WRITE_CLOCK);
  and and_5 (and_5_out, not_2_out, j_k_ff_2_q);
  assign controlled_buffer_6_out = and_5_out ? s_r_ff_1_q : 1'bz;  // Controlled_Buffer controlled_buffer_6
  assign controlled_buffer_6_out = WRITE_ENABLE ? WRITE_CLOCK : 1'bz;  // Controlled_Buffer controlled_buffer_7
  Counter #(.max('h7fff), .width(15)) counter_2 (
    .clr(monostable_1_pulse), .load(and_19_out), .count(or_5_out), .clk(controlled_buffer_6_out),
    .D(ram_2_data), .Q(counter_2_q));  // open: up, carry
  or or_5 (or_5_out, comparator_1_eq, nor_1_out);
  Counter #(.trigger("falling"), .width(15)) counter_3 (
    .clr(monostable_1_pulse), .up(or_8_out), .count(and_13_out), .clk(s_r_ff_1_q), .carry(counter_3_carry),
    .Q(counter_3_q));  // open: load, D
  Counter #(.max('h3fff), .trigger("falling"), .width(14)) counter_4 (
    .clr(monostable_1_pulse), .up(comparator_9_eq[1]), .count(or_10_out), .clk(s_r_ff_1_q), .Q(counter_4_q));  // open: load, D, carry
  not not_7 (not_7_out, controlled_buffer_3_out);
  assign ROM_WRITE_ENABLE = WRITE_ENABLE ? not_6_out : 1'bz;  // Controlled_Buffer controlled_buffer_8
  S_R_Flip_Flop s_r_ff_1 (.Q(s_r_ff_1_q), .reset(nor_4_out), .Qn(s_r_ff_1_qn), .preset(nor_3_out));  // open: S, R, clk
  nor nor_3 (nor_3_out, not_7_out, monostable_5_pulse);
  nor nor_4 (nor_4_out, controlled_buffer_3_out, monostable_4_pulse);
  monostable monostable_4 (.WAVE(s_r_ff_1_q), .PULSE(monostable_4_pulse));
  monostable monostable_5 (.WAVE(s_r_ff_1_qn), .PULSE(monostable_5_pulse));
  Comparator #(.width(4)) comparator_1 (.a(counter_1_q), .b(4'b1000), .eq(comparator_1_eq));  // open: gt, lt
  assign bit_extender_1_out = {{1{1'b0}}, counter_2_q};  // Bit_Extender bit_extender_1
  assign bit_extender_2_out = {{1{1'b0}}, counter_3_q};  // Bit_Extender bit_extender_2
  and and_6 (and_6_out, not_2_out, j_k_ff_1_qn);
  ROM #(.addrWidth(15)) rom_1 (.addr(counter_2_q), .data(rom_1_data));
  RAM #(.addrWidth(15), .asyncread("true"), .databus("bidir"), .trigger("falling")) ram_1 (
    .addr(counter_3_q), .we(and_12_out), .oe(not_8_out), .clk(s_r_ff_1_q), .data({ram_1_data_2, ram_1_data}));
  not not_8 (not_8_out, and_12_out);
  not not_9 (not_9_out, and_22_out);
  Hex_Digit_Display hex_digit_display_1 (.value(bit_extender_1_out[15:12]));  // open: dp
  Hex_Digit_Display hex_digit_display_2 (.value(bit_extender_1_out[11:8]));  // open: dp
  Hex_Digit_Display hex_digit_display_3 (.value(bit_extender_2_out[15:12]));  // open: dp
  Hex_Digit_Display hex_digit_display_4 (.value(bit_extender_2_out[11:8]));  // open: dp
  Hex_Digit_Display hex_digit_display_5 (.value(ram_1_data_2));  // open: dp
  Hex_Digit_Display hex_digit_display_6 (.value(ram_1_data));  // open: dp
  or or_6 (ROM_CHIP_ENABLE, comparator_1_eq, not_10_out);
  not not_10 (not_10_out, WRITE_ENABLE);
  assign ROM_DATA = comparator_10_eq[4] ? {8{1'b0}} : 8'bz;  // Controlled_Buffer controlled_buffer_9
  RAM #(.addrWidth(14), .asyncread("true"), .dataWidth(15), .databus("bidir"), .trigger("falling")) ram_2 (
    .addr(counter_4_q), .we(and_22_out), .oe(not_9_out), .clk(s_r_ff_1_q), .data(ram_2_data));
  Hex_Digit_Display hex_digit_display_7 (.value(bit_extender_1_out[7:4]));  // open: dp
  Hex_Digit_Display hex_digit_display_8 (.value(bit_extender_1_out[3:0]));  // open: dp
  Hex_Digit_Display hex_digit_display_9 (.value(bit_extender_2_out[7:4]));  // open: dp
  Hex_Digit_Display hex_digit_display_10 (.value(bit_extender_2_out[3:0]));  // open: dp
  assign ROM_DATA = WRITE_ENABLE ? undriven : 8'bz;  // Controlled_Buffer controlled_buffer_10
  assign ROM_DATA = and_5_out ? rom_1_data : 8'bz;  // Controlled_Buffer controlled_buffer_11
  LED led_1 (.in(comparator_9_eq[7]));
  LED led_2 (.in(comparator_9_eq[6]));
  not not_11 (not_11_out, comparator_10_eq[0]);
  assign controlled_buffer_12_out = comparator_10_eq[3] ? {8{1'b0}} : 8'bz;  // Controlled_Buffer controlled_buffer_12
  not not_12 (not_12_out, comparator_10_eq[3]);
  assign controlled_buffer_12_out = not_12_out ? ROM_DATA : 8'bz;  // Controlled_Buffer controlled_buffer_13
  LED led_3 (.in(comparator_9_eq[5]));
  LED led_4 (.in(comparator_9_eq[4]));
  LED led_5 (.in(comparator_9_eq[3]));
  LED led_6 (.in(comparator_9_eq[2]));
  and and_7 (comparator_10_eq[5], not_11_out, j_k_ff_2_q);
  Adder adder_1 (.a({ram_1_data_2, ram_1_data}), .b(8'h1), .out(adder_1_out));  // open: cin, cout
  Subtractor subtractor_1 (.a({ram_1_data_2, ram_1_data}), .b(8'h1), .out(subtractor_1_out));  // open: bin, bout
  LED led_7 (.in(comparator_9_eq[1]));
  LED led_8 (.in(comparator_9_eq[0]));
  LED led_9 (.in(comparator_10_eq[5]));
  LED led_10 (.in(comparator_10_eq[4]));
  LED led_11 (.in(comparator_10_eq[3]));
  LED led_12 (.in(AWAITING_INPUT));
  LED led_13 (.in(comparator_10_eq[1]));
  LED led_14 (.in(comparator_10_eq[0]));
  Comparator comparator_2 (.a(controlled_buffer_12_out), .b(8'h3e), .eq(comparator_9_eq[7]));  // open: gt, lt
  Comparator comparator_3 (.a(controlled_buffer_12_out), .b(8'h3c), .eq(comparator_9_eq[6]));  // open: gt, lt
  Comparator comparator_4 (.a(controlled_buffer_12_out), .b(8'h2b), .eq(comparator_9_eq[5]));  // open: gt, lt
  Comparator comparator_5 (.a(controlled_buffer_12_out), .b(8'h2d), .eq(comparator_9_eq[4]));  // open: gt, lt
  Comparator comparator_6 (.a(controlled_buffer_12_out), .b(8'h2e), .eq(comparator_9_eq[3]));  // open: gt, lt
  Comparator comparator_7 (.a(controlled_buffer_12_out), .b(8'h2c), .eq(comparator_9_eq[2]));  // open: gt, lt
  Comparator comparator_8 (.a(ROM_DATA), .b(8'h5b), .eq(comparator_9_eq[1]));  // open: gt, lt
  Comparator comparator_9 (.a(ROM_DATA), .b(8'h5d), .eq(comparator_9_eq[0]));  // open: gt, lt
  Comparator comparator_10 (.a(ROM_DATA), .b({8{1'b0}}), .eq(comparator_10_eq[0]));  // open: gt, lt
  and and_8 (and_8_out, and_6_out, and_12_out);
  and and_9 (and_9_out, comparator_9_eq[2], and_12_out);
  and and_10 (and_10_out, comparator_9_eq[5], and_12_out);
  and and_11 (and_11_out, comparator_9_eq[4], and_12_out);
  Register register_1 (.D(adder_1_out), .clk(s_r_ff_1_q), .Q(register_1_q));  // open: en, clr
  Register register_2 (.D(subtractor_1_out), .clk(s_r_ff_1_q), .Q(register_2_q));  // open: en, clr
  assign ram_2_data = and_22_out ? counter_2_q : 15'bz;  // Controlled_Buffer controlled_buffer_14
  or or_7 (or_7_out, and_6_out, comparator_9_eq[5], comparator_9_eq[4], comparator_9_eq[2]);
  assign {ram_1_data_2, ram_1_data} = and_8_out ? {8{1'b0}} : 8'bz;  // Controlled_Buffer controlled_buffer_15
  assign {ram_1_data_2, ram_1_data} = and_9_out ? R_IN_q : 8'bz;  // Controlled_Buffer controlled_buffer_16
  assign {ram_1_data_2, ram_1_data} = and_10_out ? register_1_q : 8'bz;  // Controlled_Buffer controlled_buffer_17
  assign {ram_1_data_2, ram_1_data} = and_11_out ? register_2_q : 8'bz;  // Controlled_Buffer controlled_buffer_18
  or or_8 (or_8_out, and_6_out, comparator_9_eq[7]);
  and and_12 (and_12_out, or_7_out, nor_2_out);
  or or_9 (or_9_out, or_8_out, comparator_9_eq[6]);
  and and_13 (and_13_out, or_9_out, nor_2_out);
  monostable monostable_6 (.WAVE(pull_resistor_8_node[2]), .PULSE(monostable_6_pulse));
  or or_10 (or_10_out, comparator_9_eq[0], comparator_9_eq[1]);
  and and_14 (and_14_out, comparator_10_eq[1], monostable_6_pulse);
  and and_15 (and_15_out, comparator_10_eq[1], j_k_ff_3_q);
  and and_16 (and_16_out, j_k_ff_4_qn, comparator_9_eq[3]);
  and and_17 (and_17_out, AWAITING_INPUT, j_k_ff_5_q);
  and and_18 (and_18_out, comparator_9_eq[2], j_k_ff_6_qn);
  Comparator comparator_11 (.a({ram_1_data_2, ram_1_data}), .b({8{1'b0}}), .eq(comparator_11_eq));  // open: gt, lt
  J_K_Flip_Flop #(.trigger("falling")) j_k_ff_3 (
    .J(1'b0), .K(j_k_ff_3_q), .clk(s_r_ff_1_q), .Q(j_k_ff_3_q), .preset(and_14_out),
    .reset(monostable_1_pulse));  // open: Qn
  J_K_Flip_Flop #(.trigger("falling")) j_k_ff_4 (
    .J(and_16_out), .K(and_15_out), .clk(s_r_ff_1_q), .Q(comparator_10_eq[1]), .Qn(j_k_ff_4_qn),
    .reset(monostable_1_pulse));  // open: preset
  Register #(.trigger("falling")) R_OUT (
    .D({ram_1_data_2, ram_1_data}), .en(and_16_out), .clk(s_r_ff_1_q), .Q(R_OUT_q));  // open: clr
  Register R_IN (.D(controlled_buffer_19_out), .en(AWAITING_INPUT), .clk(monostable_7_pulse), .Q(R_IN_q));  // open: clr
  J_K_Flip_Flop #(.trigger("falling")) j_k_ff_5 (
    .J(1'b0), .K(and_17_out), .clk(s_r_ff_1_q), .Q(j_k_ff_5_q), .Qn(j_k_ff_5_qn),
    .preset(monostable_7_pulse), .reset(monostable_1_pulse));
  J_K_Flip_Flop #(.trigger("falling")) j_k_ff_6 (
    .J(and_18_out), .K(and_17_out), .clk(s_r_ff_1_q), .Q(AWAITING_INPUT), .Qn(j_k_ff_6_qn),
    .reset(monostable_1_pulse));  // open: preset
  not not_13 (not_13_out, comparator_11_eq);
  and and_19 (and_19_out, not_13_out, comparator_9_eq[0]);
  assign controlled_buffer_19_out = comparator_9_eq[3] ? R_OUT_q : 8'bz;  // Controlled_Buffer controlled_buffer_19
  and and_20 (and_20_out, AWAITING_INPUT, j_k_ff_5_qn);
  and and_21 (and_21_out, j_k_ff_7_qn, comparator_11_eq, comparator_9_eq[1]);
  and and_22 (and_22_out, comparator_9_eq[1], not_13_out);
  Pull_Resistor pull_resistor_8 (.node(pull_resistor_8_node[2]));
  assign OUTPUT_READY = comparator_9_eq[3] ? comparator_10_eq[1] : 1'bz;  // Controlled_Buffer controlled_buffer_20
  and and_23 (and_23_out, comparator_10_eq[3], comparator_9_eq[0], comparator_12_eq);
  Adder #(.width(14)) adder_2 (.a(counter_4_q), .b(14'h1), .out(adder_2_out));  // open: cin, cout
  Pull_Resistor pull_resistor_9 (.node(pull_resistor_9_node));
  assign pull_resistor_9_node = AWAITING_INPUT ? OUTPUT_READY : 1'bz;  // Controlled_Buffer controlled_buffer_21
  monostable monostable_7 (.WAVE(pull_resistor_9_node), .PULSE(monostable_7_pulse));
  J_K_Flip_Flop #(.trigger("falling")) j_k_ff_7 (
    .J(and_21_out), .K(and_23_out), .clk(s_r_ff_1_q), .Q(comparator_10_eq[3]), .Qn(j_k_ff_7_qn),
    .reset(monostable_1_pulse));  // open: preset
  Register #(.trigger("falling"), .width(14)) Jump_Snapshot (
    .D(adder_2_out), .en(and_21_out), .clk(s_r_ff_1_q), .Q(Jump_Snapshot_q));  // open: clr
  Comparator #(.width(14)) comparator_12 (.a(Jump_Snapshot_q), .b(counter_4_q), .eq(comparator_12_eq));  // open: gt, lt
  monostable monostable_8 (.WAVE(PUSH_INPUT_out[0]), .PULSE(monostable_8_pulse));
  assign {controlled_buffer_19_out, OUTPUT_READY} = AWAITING_INPUT ? PUSH_INPUT_out : 9'bz;  // Controlled_Buffer controlled_buffer_22
  Keyboard keyboard_1 (.clk(monostable_8_pulse), .clr(EXT_RESET_out), .data(keyboard_1_data));  // open: re, avail
  Button PUSH_INPUT (.out(PUSH_INPUT_out[0]));
  Button OUTPUT_CONFIRMED (.out(pull_resistor_8_node[2]));
  assign PUSH_INPUT_out[8:1] = {{1{1'b0}}, keyboard_1_data};  // Bit_Extender bit_extender_3
  Bit_Extender #(.out_width(7), .\type ("zero")) bit_extender_4 (
    .in(controlled_buffer_19_out), .out(bit_extender_4_out));
  TTY tty_1 (.data(bit_extender_4_out), .clk(pull_resistor_8_node[2]), .we(OUTPUT_READY), .clr(EXT_RESET_out));
  Button EXT_RESET (.out(EXT_RESET_out));

  // Notes on the sheet:
  //   ENABLED
  //   STARTUP
  //   clock filter
  //   Program Counter
  //   Cell Pointer
  //   contents of rom_1 (hex, n*v repeats v):
  //   3e 2c 5b 48*2d 3e 10*2b 3c 3c 5b 2d 3e 3e 3e 2b 3c 3c 3c 5d 3e 3e 5b 2d 3e 5b d a 2d 3e 2b 4*3c 2b
  //   3e 3e 3e 5d 3e 5b 2d 3c 2b 3e 5d 3c 3c 5d 3e 5b 2d 5d 3c 3c 5b 2d 3c 2b 3e 5d 2c 5d 2b 3c 2d 5b 2b
  //   3e 2b 3c 5b 2d 3e 3e 2b 3e 2b 3c 3c 3c 5d 3e 3e 3e 5b 2d 3c 3c 3c 2b 3e 3e 3e 5d 3e 2b 5b 5b 2d 3c
  //   2b 3c 2d 3c 2d 5b d a 2d 4*3e 2b 3e 2b 5*3c 5d 5*3e 5b 2d 5*3c 2b 5*3e 5d 3c 5b 3c 2b 3e 5b 2d 5d 5d
  //   3c 5b 2d 3e 2b 3e 2b 3c 3c 5d 3e 3e 5b 2d 3c 3c 2b 3e 3e 5d 3c 5b 5b 2d 5d 3c 2d 3c 3c 5b 2d 3e 3e
  //   3e 2b 3e 2b 3c d a 3c 3c 3c 5d 4*3e 5b 2d 4*3c 2b 4*3e 5d 3c 5b 3c 2b 3e 5b 2d 5d 5d 5d 3c 5d 3c 3c
  //   5b 2d 3e 3e 3e 2b 3e 2b 4*3c 5d 4*3e 5b 2d 4*3c 2b 4*3e 5d 3c 5b 3c 2b 3e 5b 2d 5d 5d 3c 5b 2d 3e 2b
  //   3e 2b 3c d a 3c 5d 3e 3e 5b 2d 3c 3c 2b 3e 3e 5d 3c 5b 3c 3c 5b 2d 3c 3c 2b 3e 3e 5d 3e 3e 5b 2d 5d
  //   5d 3c 5d 2b 3c 3c 3c 5b 2d 4*3e 2b 3e 2b 5*3c 5d 5*3e 5b 2d 5*3c 2b 5*3e 5d 3c 5b 3c 2d 3e 5b 2d 5d
  //   5d 3c d a 3c 5b 2d 3c 3c 2b 3e 3e 5d 3e 5b 2d 3c 2b 3e 5d 3c 5b 2d 3c 3c 3c 5b 3e 3e 2b 3c 5b 2d 3c
  //   2d 3e 3e 3e 2b 3c 3c 5d 3e 3e 5b 2d 3c 3c 2b 3e 3e 5d 3c 3c 3c 5d 3e 3e 5b 2d 3c 3c 2b 3e 3e 5d 3c
  //   5b 2d 3e 2b 3e 2b 3c 3c 5d 3e 3e 5b 2d 3c 3c 2b 3e d a 3e 5d 2b 5b 3e 10*2b 5b 3c 3c 5b 2d 3e 3e 3e
  //   2b 3e 2b 4*3c 5d 4*3e 5b 2d 4*3c 2b 4*3e 5d 3c 5b 3c 3c 3c 2d 3e 3e 3e 5b 2d 5d 5d 3c 2d 5d 3e 3e 3e
  //   2b 4*3c 2d 5d 4*3e 5b 2d 3c d a 3c 3c 3c 2b 4*3e 5d 5*3c 5b 5b 2d 5d 3e 5b 2d 3e 10*2b 3c 5d 3e 5b
  //   2d 3c 2b 3e 5d 3c 3c 3c 5b 2d 3e 2b 3e 3e 2b 3c 3c 3c 5d 3e 3e 3e 5b 2d 3c 3c 3c 2b 3e 3e 3e 5d 3c
  //   5b 3e 9*2b d a 2b 5b 3c 3c 5b 2d 3e 3e 3e 2b 3e 2b 4*3c 5d 4*3e 5b 2d 4*3c 2b 4*3e 5d 3c 5b 3c 3c 3c
  //   2d 3e 3e 3e 5b 2d 5d 5d 3c 2d 5d 3e 3e 3e 2b 4*3c 2d 5d 4*3e 5b 2d 4*3c 2b 4*3e 5d 5*3c d a 5d 3c 5b
  //   2d 3e 2b 3e 3e 2b 3c 3c 3c 5d 3e 3e 3e 5b 2d 3c 3c 3c 2b 3e 3e 3e 5d 3c 2d 5b 2b 3e 3e 3e 2b 5b 5b
  //   2d 3c 3c 2b 3c 2d 3c 2d 3e 5b 2d 4*3e 2b 3e 2b 5*3c 5d 5*3e 5b 2d 5*3c 2b 5*3e 5d 3c d a 5b 3c 2b 3e
  //   5b 2d 5d 5d 3c 5b 2d 3e 2b 3e 2b 3c 3c 5d 3e 3e 5b 2d 3c 3c 2b 3e 3e 5d 3c 5b 5b 2d 5d 3c 2d 4*3c 5b
  //   2d 5*3e 2b 3e 2b 6*3c 5d 6*3e 5b 2d 6*3c 2b 6*3e 5d 3c 5b d a 3c 2b 3e 5b 2d 5d 5d 5d 3c 5d 2b 3c 3c
  //   3c 5b 2d 4*3e 2b 3e 2b 5*3c 5d 5*3e 5b 2d 5*3c 2b 5*3e 5d 3c 5b 5b 2d 5d 3c 2d 3e 5d 3c 5b 2d 3e 2b
  //   3e 2b 3c 3c 5d 3e 3e 5b 2d 3c 3c 2b 3e 3e 5d 3c 5b 5b d a 2d 5d 3c 3c 2b 3c 5b 2d 3c 2b 3e 5d 3e 3e
  //   3e 5d 3c 5d 3c 48*2b 2e 5b 2d 5d 3c 5b 2d 3c 2b 3c 2b 3e 3e d a 5d 3c 5b 10*2d 3e 2b 3c 5d 3e 5b 2d
  //   3c 2b 3e 5d 3c 2d 5d 3c 48*2b 2e 5b 2d 5d d a 10*2b 2e 5b 2d 5d 3c 3c 5b 2d 3e 3e 2b 3e 2b 3c 3c 3c
  //   5d 3e 3e 3e 5b 2d 3c 3c 3c 2b 3e 3e 3e 5d 3e 2b 5b 5b 2d 3c 2b 3c 2d 3c 2d 5b 2d 4*3e 2b 3e 2b 5*3c
  //   5d 5*3e 5b 2d 5*3c 2b 3e d a 4*3e 5d 3c 5b 3c 2b 3e 5b 2d 5d 5d 3c 5b 2d 3e 2b 3e 2b 3c 3c 5d 3e 3e
  //   5b 2d 3c 3c 2b 3e 3e 5d 3c 5b 5b 2d 5d 3c 2d 3c 3c 5b 2d 3e 3e 3e 2b 3e 2b 4*3c 5d 4*3e 5b 2d 4*3c
  //   2b 4*3e 5d 3c 5b 3c 2b 3e 5b 2d 5d d a 5d 5d 3c 5d 3c 3c 5b 2d 3e 3e 3e 2b 3e 2b 4*3c 5d 4*3e 5b 2d
  //   4*3c 2b 4*3e 5d 3c 5b 3c 2b 3e 5b 2d 5d 5d 3c 5b 2d 3e 2b 3e 2b 3c 3c 5d 3e 3e 5b 2d 3c 3c 2b 3e 3e
  //   5d 3c 5b 3c 3c 5b 2d 3c 3c 2b 3e 3e 5d 3e 3e 5b 2d d a 5d 5d 3c 5d 2b 3c 3c 3c 5b 2d 4*3e 2b 3e 2b
  //   5*3c 5d 5*3e 5b 2d 5*3c 2b 5*3e 5d 3c 5b 3c 2d 3e 5b 2d 5d 5d 3c 3c 5b 2d 3c 3c 2b 3e 3e 5d 3e 5b 2d
  //   3c 2b 3e 5d 3c 5d 3c 3c 3c 2d 5d 3e 5b 2d 5d 3c
  //   Cell Value
  //   >
  //   <
  //   waiting for output confirmation
  //   -
  //   +
  //   .
  //   ,
  //   running
  //   starting
  //   jumping
  //   waiting for input
  //   finished
  //   >
  //   <
  //   +
  //   -
  //   .
  //   ,
  //   [
  //   ]
  //   \0
  //   [
  //   ]
  //   OE
  //   State OUTPUT
  //   IE
  //   State INPUT
  //   State JUMPING
endmodule

module monostable (
  input  WAVE,
  output PULSE
);

  wire and_1_out, clock_1_out, clock_2_out, j_k_ff_1_qn, j_k_ff_2_qn, not_1_out;

  not not_1 (not_1_out, WAVE);
  and and_1 (and_1_out, not_1_out, WAVE);
  Clock clock_1 (.out(clock_1_out));
  Clock clock_2 (.out(clock_2_out));
  J_K_Flip_Flop j_k_ff_1 (
    .J(1'b0), .K(1'b1), .clk(clock_1_out), .Qn(j_k_ff_1_qn), .preset(and_1_out));  // open: Q, reset
  J_K_Flip_Flop #(.trigger("falling")) j_k_ff_2 (
    .J(1'b0), .K(1'b1), .clk(clock_2_out), .Qn(j_k_ff_2_qn), .preset(and_1_out));  // open: Q, reset
  nor nor_1 (PULSE, j_k_ff_1_qn, j_k_ff_2_qn);
endmodule

module slow_clock (
  input  RESET,
  output out_2
);

  wire clock_1_out, clock_2_out, counter_1_carry;

  Clock clock_1 (.out(clock_1_out));
  Counter #(.max('h1f3), .width(10)) counter_1 (
    .clr(RESET), .clk(clock_1_out), .carry(counter_1_carry));  // open: load, up, count, D, Q
  T_Flip_Flop t_ff_1 (.T(counter_1_carry), .clk(clock_2_out), .Q(out_2), .reset(RESET));  // open: Qn, preset
  Clock clock_2 (.out(clock_2_out));
endmodule

module displaydriver (
  input  [3:0] SEL,
  input  [15:0] PC,
  input  [6:0] SEGMENTS,
  input  [15:0] ADDR,
  input  [7:0] DATA,
  output [3:0] VAL
);

  wire demultiplexer_1_out0, demultiplexer_1_out1, demultiplexer_1_out2, demultiplexer_2_out0,
       demultiplexer_2_out1, demultiplexer_2_out2, demultiplexer_2_out3, demultiplexer_3_out0,
       demultiplexer_3_out1, demultiplexer_3_out2, demultiplexer_3_out3, demultiplexer_4_out0,
       demultiplexer_4_out1, multiplexer_1_out, multiplexer_2_out, multiplexer_3_out, multiplexer_4_out,
       multiplexer_5_out, multiplexer_6_out, multiplexer_7_out, multiplexer_8_out, multiplexer_9_out,
       multiplexer_10_out, multiplexer_11_out, multiplexer_12_out;
  wire [6:0] controlled_buffer_1_out, controlled_buffer_2_out, controlled_buffer_3_out,
       controlled_buffer_4_out, controlled_buffer_5_out, controlled_buffer_6_out, controlled_buffer_7_out,
       controlled_buffer_8_out, controlled_buffer_9_out, controlled_buffer_10_out;

  Multiplexer #(.select(2)) multiplexer_1 (
    .in0(PC[0]), .in1(PC[4]), .in2(PC[8]), .in3(PC[12]), .out(multiplexer_1_out), .sel(SEL[1:0]));
  Multiplexer #(.select(2)) multiplexer_2 (
    .in0(PC[1]), .in1(PC[5]), .in2(PC[9]), .in3(PC[13]), .out(multiplexer_2_out), .sel(SEL[1:0]));
  Multiplexer #(.select(2)) multiplexer_3 (
    .in0(PC[2]), .in1(PC[6]), .in2(PC[10]), .in3(PC[14]), .out(multiplexer_3_out), .sel(SEL[1:0]));
  Multiplexer #(.select(2)) multiplexer_4 (
    .in0(PC[3]), .in1(PC[7]), .in2(PC[11]), .in3(PC[15]), .out(multiplexer_4_out), .sel(SEL[1:0]));
  Multiplexer #(.select(2)) multiplexer_5 (
    .in0(ADDR[0]), .in1(ADDR[4]), .in2(ADDR[8]), .in3(ADDR[12]), .out(multiplexer_5_out), .sel(SEL[1:0]));
  Multiplexer #(.select(2)) multiplexer_6 (
    .in0(ADDR[1]), .in1(ADDR[5]), .in2(ADDR[9]), .in3(ADDR[13]), .out(multiplexer_6_out), .sel(SEL[1:0]));
  Multiplexer #(.select(2)) multiplexer_7 (
    .in0(ADDR[2]), .in1(ADDR[6]), .in2(ADDR[10]), .in3(ADDR[14]), .out(multiplexer_7_out), .sel(SEL[1:0]));
  Multiplexer #(.select(2)) multiplexer_8 (
    .in0(ADDR[3]), .in1(ADDR[7]), .in2(ADDR[11]), .in3(ADDR[15]), .out(multiplexer_8_out), .sel(SEL[1:0]));
  Multiplexer #(.select(2)) multiplexer_9 (
    .in0(DATA[0]), .in1(DATA[4]), .out(multiplexer_9_out), .sel(SEL[1:0]));  // open: in2, in3
  Multiplexer #(.select(2)) multiplexer_10 (
    .in0(DATA[1]), .in1(DATA[5]), .out(multiplexer_10_out), .sel(SEL[1:0]));  // open: in2, in3
  Multiplexer #(.select(2)) multiplexer_11 (
    .in0(DATA[2]), .in1(DATA[6]), .out(multiplexer_11_out), .sel(SEL[1:0]));  // open: in2, in3
  Multiplexer #(.select(2)) multiplexer_12 (
    .in0(DATA[3]), .in1(DATA[7]), .out(multiplexer_12_out), .sel(SEL[1:0]));  // open: in2, in3
  Multiplexer #(.select(2)) multiplexer_13 (
    .in0(multiplexer_1_out), .in1(multiplexer_5_out), .in2(multiplexer_9_out), .out(VAL[0]), .sel(SEL[3:2]));  // open: in3
  Multiplexer #(.select(2)) multiplexer_14 (
    .in0(multiplexer_2_out), .in1(multiplexer_6_out), .in2(multiplexer_10_out), .out(VAL[1]), .sel(SEL[3:2]));  // open: in3
  Multiplexer #(.select(2)) multiplexer_15 (
    .in0(multiplexer_3_out), .in1(multiplexer_7_out), .in2(multiplexer_11_out), .out(VAL[2]), .sel(SEL[3:2]));  // open: in3
  Multiplexer #(.select(2)) multiplexer_16 (
    .in0(multiplexer_4_out), .in1(multiplexer_8_out), .in2(multiplexer_12_out), .out(VAL[3]), .sel(SEL[3:2]));  // open: in3
  Demultiplexer #(.select(2)) demultiplexer_1 (
    .out0(demultiplexer_1_out0), .out1(demultiplexer_1_out1), .out2(demultiplexer_1_out2), .in(1'b1),
    .sel(SEL[3:2]));  // open: out3
  Demultiplexer #(.select(2)) demultiplexer_2 (
    .out0(demultiplexer_2_out0), .out1(demultiplexer_2_out1), .out2(demultiplexer_2_out2),
    .out3(demultiplexer_2_out3), .in(demultiplexer_1_out0), .sel(SEL[1:0]));
  Demultiplexer #(.select(2)) demultiplexer_3 (
    .out0(demultiplexer_3_out0), .out1(demultiplexer_3_out1), .out2(demultiplexer_3_out2),
    .out3(demultiplexer_3_out3), .in(demultiplexer_1_out1), .sel(SEL[1:0]));
  Demultiplexer #(.select(2)) demultiplexer_4 (
    .out0(demultiplexer_4_out0), .out1(demultiplexer_4_out1), .in(demultiplexer_1_out2), .sel(SEL[1:0]));  // open: out2, out3
  assign controlled_buffer_1_out = demultiplexer_2_out0 ? SEGMENTS : 7'bz;  // Controlled_Buffer controlled_buffer_1
  assign controlled_buffer_2_out = demultiplexer_2_out1 ? SEGMENTS : 7'bz;  // Controlled_Buffer controlled_buffer_2
  assign controlled_buffer_3_out = demultiplexer_2_out2 ? SEGMENTS : 7'bz;  // Controlled_Buffer controlled_buffer_3
  assign controlled_buffer_4_out = demultiplexer_2_out3 ? SEGMENTS : 7'bz;  // Controlled_Buffer controlled_buffer_4
  assign controlled_buffer_5_out = demultiplexer_3_out0 ? SEGMENTS : 7'bz;  // Controlled_Buffer controlled_buffer_5
  assign controlled_buffer_6_out = demultiplexer_3_out1 ? SEGMENTS : 7'bz;  // Controlled_Buffer controlled_buffer_6
  assign controlled_buffer_7_out = demultiplexer_3_out2 ? SEGMENTS : 7'bz;  // Controlled_Buffer controlled_buffer_7
  assign controlled_buffer_8_out = demultiplexer_3_out3 ? SEGMENTS : 7'bz;  // Controlled_Buffer controlled_buffer_8
  assign controlled_buffer_9_out = demultiplexer_4_out0 ? SEGMENTS : 7'bz;  // Controlled_Buffer controlled_buffer_9
  assign controlled_buffer_10_out = demultiplexer_4_out1 ? SEGMENTS : 7'bz;  // Controlled_Buffer controlled_buffer_10
  _7_Segment_Display u_7_segment_display_1 (
    .g(controlled_buffer_4_out[3]), .f(controlled_buffer_4_out[2]), .a(controlled_buffer_4_out[1]),
    .b(controlled_buffer_4_out[0]), .e(controlled_buffer_4_out[6]), .d(controlled_buffer_4_out[5]),
    .c(controlled_buffer_4_out[4]));  // open: dp
  _7_Segment_Display u_7_segment_display_2 (
    .g(controlled_buffer_8_out[3]), .f(controlled_buffer_8_out[2]), .a(controlled_buffer_8_out[1]),
    .b(controlled_buffer_8_out[0]), .e(controlled_buffer_8_out[6]), .d(controlled_buffer_8_out[5]),
    .c(controlled_buffer_8_out[4]));  // open: dp
  _7_Segment_Display u_7_segment_display_3 (
    .g(controlled_buffer_10_out[3]), .f(controlled_buffer_10_out[2]), .a(controlled_buffer_10_out[1]),
    .b(controlled_buffer_10_out[0]), .e(controlled_buffer_10_out[6]), .d(controlled_buffer_10_out[5]),
    .c(controlled_buffer_10_out[4]));  // open: dp
  _7_Segment_Display u_7_segment_display_4 (
    .g(controlled_buffer_3_out[3]), .f(controlled_buffer_3_out[2]), .a(controlled_buffer_3_out[1]),
    .b(controlled_buffer_3_out[0]), .e(controlled_buffer_3_out[6]), .d(controlled_buffer_3_out[5]),
    .c(controlled_buffer_3_out[4]));  // open: dp
  _7_Segment_Display u_7_segment_display_5 (
    .g(controlled_buffer_2_out[3]), .f(controlled_buffer_2_out[2]), .a(controlled_buffer_2_out[1]),
    .b(controlled_buffer_2_out[0]), .e(controlled_buffer_2_out[6]), .d(controlled_buffer_2_out[5]),
    .c(controlled_buffer_2_out[4]));  // open: dp
  _7_Segment_Display u_7_segment_display_6 (
    .g(controlled_buffer_7_out[3]), .f(controlled_buffer_7_out[2]), .a(controlled_buffer_7_out[1]),
    .b(controlled_buffer_7_out[0]), .e(controlled_buffer_7_out[6]), .d(controlled_buffer_7_out[5]),
    .c(controlled_buffer_7_out[4]));  // open: dp
  _7_Segment_Display u_7_segment_display_7 (
    .g(controlled_buffer_6_out[3]), .f(controlled_buffer_6_out[2]), .a(controlled_buffer_6_out[1]),
    .b(controlled_buffer_6_out[0]), .e(controlled_buffer_6_out[6]), .d(controlled_buffer_6_out[5]),
    .c(controlled_buffer_6_out[4]));  // open: dp
  _7_Segment_Display u_7_segment_display_8 (
    .g(controlled_buffer_9_out[3]), .f(controlled_buffer_9_out[2]), .a(controlled_buffer_9_out[1]),
    .b(controlled_buffer_9_out[0]), .e(controlled_buffer_9_out[6]), .d(controlled_buffer_9_out[5]),
    .c(controlled_buffer_9_out[4]));  // open: dp
  _7_Segment_Display u_7_segment_display_9 (
    .g(controlled_buffer_1_out[3]), .f(controlled_buffer_1_out[2]), .a(controlled_buffer_1_out[1]),
    .b(controlled_buffer_1_out[0]), .e(controlled_buffer_1_out[6]), .d(controlled_buffer_1_out[5]),
    .c(controlled_buffer_1_out[4]));  // open: dp
  _7_Segment_Display u_7_segment_display_10 (
    .g(controlled_buffer_5_out[3]), .f(controlled_buffer_5_out[2]), .a(controlled_buffer_5_out[1]),
    .b(controlled_buffer_5_out[0]), .e(controlled_buffer_5_out[6]), .d(controlled_buffer_5_out[5]),
    .c(controlled_buffer_5_out[4]));  // open: dp
endmodule
